# Fritzing sketch Fritzing (saved by Fritzing 0.9.3b)
breadboards: 1

parts:
  PSU1 = Adjustable Breadboard Power Supply
  Q1 = TIP120 Hi-Current Darlington Transistor
  Part2 = Adafruit Breadboard-Friendly NeoPixel [part_number="Adafruit #1312"]
  Part3 = Adafruit Pro Trinket 5V 16MHz [part_number="Adafruit #2000"]
  hc-sr1 = hc-sr04
  R1 = Resistor [tolerance=±5% resistance=220 package="1206 [SMD]"]
  Squirt_Gun_Motor = DC Motor
  D1 = Rectifier Diode [part_number=1N4001 package="Melf DO-213 AB [SMD]"]

nets:
  VDD: PSU1.Vout+, Part2.VDD, Part3.+5V, hc-sr1.VCC
  GND: PSU1.Vout-, Part2.GND, Part3.GND, hc-sr1.GND
  N1: PSU1.Vin+, Squirt_Gun_Motor.pin_2, D1.cathode
  N2: PSU1.Vin-, Q1.EMITTER
  N3: Q1.BASE, R1.Pin_1
  N4: Q1.COLLECTOR, Squirt_Gun_Motor.pin_1, D1.anode
  N5: Part2.IN, Part3.D4
  N6: Part3.D6, hc-sr1.Echo
  N7: Part3.D5, hc-sr1.Trig
  N8: Part3.D9, R1.Pin_0

custom parts:
  Adafruit Breadboard-Friendly NeoPixel: This is the easiest way possible to add small, bright RGB pixels to your project. We took the same technology from our Flora NeoPixels and made them breadboard friendly, with two rows of 3 x 0.1" spaced header on each side for easy soldering, chaining and breadboarding. These ultra-bright LEDs have a constant-current driver cooked right into the LED package! The pixels are chainable - so you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
  Adafruit Pro Trinket 5V 16MHz: Trinket's got a big sister in town - the Pro Trinket 5V! Pro Trinket combines everything you love about Trinket with the familiarity of the common core Arduino chip, the ATmega328. It's like an Arduino Pro Mini with more pins and USB tossed in, so delicious. Trinket's a year old now, and while its been great to see tons of tiny projects, sometimes you just need more pins, more FLASH, and more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
